# Fritzing sketch dht11-sdcard-nodemcu (saved by Fritzing 0.9.3b)
breadboards: 1

parts:
  U1 = NodeMCU V1.0
  Part1 = Adafruit MicroSD card breakout board [part_number="Adafruit #254"]
  DHT1 = DHT11 Humitidy and Temperature Sensor
  Squix1 = OLED 0.96" 128x64 I2C SSD1306

nets:
  N1: U1.D1, Squix1.SCL
  N2: U1.D2, Squix1.SCA
  N3: U1.D3, DHT1.DATA
  3V3: U1.3V3, Part1.+3V3, DHT1.VDD, Squix1.VCC
  GND: U1.GND, Part1.GND, DHT1.GND, Squix1.GND
  N4: U1.D5, Part1.CLK
  N5: U1.D6, Part1.DO
  N6: U1.D7, Part1.DI
  N7: U1.D8, Part1.CS

custom parts:
  NodeMCU V1.0: ESP8266 based NodeMCU
  Adafruit MicroSD card breakout board: Not just a simple breakout board, this microSD adapter goes the extra mile - designed for ease of use. Onboard 5v->3v regulator provides 150mA for power-hungry cards 3v level shifting means you can use this with ease on either 3v or 5v systems Uses a proper level shifting chip, not resistors: less problems, and faster read/write access Use 3 or 4 digital pins to read and write 2Gb+ of storage!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
  DHT11 Humitidy and Temperature Sensor: DHT11 Humidity and Temperature Sensor
